# Fritzing sketch schematic (saved by Fritzing 0.9.3b)

parts:
  WiFi-Witty-Gizwits-ESP-12F1 = WiFi-Witty-Gizwits-ESP-12F
  IR1 = TSOP312.., 314.. [package=THT]
  J1 = DIN8 [package=din8]  # not connected
  Q2 = NPN-Transistor [package="TO92 [THT]"]
  R1 = Resistor [tolerance=±5% resistance=1k package="0603 [SMD]"]
  R2 = Resistor [tolerance=±5% resistance=1k package="0603 [SMD]"]

nets:
  N1: WiFi-Witty-Gizwits-ESP-12F1.GPIO14, IR1.GND
  N2: WiFi-Witty-Gizwits-ESP-12F1.VCC, IR1.Data
  N3: WiFi-Witty-Gizwits-ESP-12F1.GND, IR1.Vs, Q2.E
  N4: WiFi-Witty-Gizwits-ESP-12F1.GPIO4, R1.Pin_0
  N5: Q2.B, R1.Pin_1
  N6: Q2.C, R2.Pin_0

custom parts:
  WiFi-Witty-Gizwits-ESP-12F: A breadboard friendly two part WiFi development board by Gizwits, powered by an ESP8266 ESP-12F SoC, featuring twin micro-usb ports, a photoresistor, a WS2812 RGB-LED and three buttons. The board comes in two parts. The bottom half has reset and flash buttons, a micro-usb with CH340 UART and 2x 1x08 female headers. The top half has the ESP-12F, LDR, RGB-LED, micro-usb (for power only), an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
  DIN8: DIN8 connector
